# Fritzing sketch Catan-ESP32-schematic-diagram (saved by Fritzing 1.0.1rc)

parts:
  C1 = Capacitor Polarized [package=cpol-radial-1000uf-25v]
  S1 = Pushbutton [package="[THT]"]
  R1 = Resistor [tolerance=±5% resistance=220 package="0805 [SMD]"]
  R2 = Resistor [tolerance=±5% resistance=220 package="0805 [SMD]"]
  Grove1 = Grove 4 Digit Display
  Grove2 = Grove OLED 128x96
  RGB_SMD_LED1 = SMD RGB LED (WS2812) [package=5050]
  RGB_SMD_LED2 = SMD RGB LED (WS2812) [package=5050]  # not connected
  RGB_SMD_LED3 = SMD RGB LED (WS2812) [package=5050]  # not connected
  RGB_SMD_LED4 = SMD RGB LED (WS2812) [package=5050]
  RGB_SMD_LED5 = SMD RGB LED (WS2812) [package=5050]
  RGB_SMD_LED6 = SMD RGB LED (WS2812) [package=5050]  # not connected
  RGB_SMD_LED7 = SMD RGB LED (WS2812) [package=5050]  # not connected
  RGB_SMD_LED8 = SMD RGB LED (WS2812) [package=5050]
  RGB_SMD_LED9 = SMD RGB LED (WS2812) [package=5050]
  Mod1 = Heltec WiFi LoRa 32 V2 [part_number=HTIT-WB32LA]
  Grove3 = Grove OLED 128x96
  Grove4 = Grove 4 Digit Display
  S2 = Pushbutton [package="[THT]"]
  R3 = Resistor [tolerance=±5% resistance=220 package="0805 [SMD]"]
  S3 = Toggle Switch [package=THT]
  R4 = Resistor [tolerance=±5% resistance=220 package="0805 [SMD]"]
  C2 = Capacitor Polarized [package=cpol-radial-1000uf-25v]

nets:
  N1: C1.+, RGB_SMD_LED1.VCC, Mod1.pin_20, R3.Pin_0, R4.Pin_1
  GND: C1.-, S1.Pin_3, S1.Pin_4, Grove1.GND, Grove2.GND, RGB_SMD_LED1.DOut, Mod1.GND, Grove3.GND, Grove4.GND, S2.Pin_3, S2.Pin_4, S3.L1, C2.-
  N2: S1.Pin_1, S1.Pin_2, R1.Pin_1, Mod1.pin_28
  VCC: R1.Pin_0, Grove1.VCC, Grove2.VCC, Grove3.VCC, Grove4.VCC, C2.+
  N3: R2.Pin_0, Mod1.pin_4
  N4: R2.Pin_1, RGB_SMD_LED1.DIn
  N5: Grove1.DIO, Mod1.pin_23, Grove4.DIO
  N6: Grove1.CLK, Mod1.pin_24, Grove4.CLK
  N7: Grove2.SDA, Mod1.pin_1, Grove3.SDA
  N8: Grove2.SCL, Mod1.pin_27, Grove3.SCL
  N9: RGB_SMD_LED4.NC, RGB_SMD_LED5.VCC
  N10: RGB_SMD_LED4.VDD, RGB_SMD_LED5.DIn
  N11: RGB_SMD_LED4.VSS, RGB_SMD_LED5.DOut
  N12: RGB_SMD_LED8.NC, RGB_SMD_LED9.VCC
  N13: RGB_SMD_LED8.VDD, RGB_SMD_LED9.DIn
  N14: Mod1.pin_31, S3.COM
  N15: Mod1.pin_32, S2.Pin_1, S2.Pin_2, R3.Pin_1
  N16: S3.L2, R4.Pin_0

notes:
  131 LEDs
  0x78 IIC
  0x7A IIC
  1000 uF
  470 uF
  1k ohm
